# Fritzing sketch Wiring (saved by Fritzing 0.9.3b)
breadboards: 1

parts:
  Part1 = Arduino Mega ADK (Rev3)
  J1 = Basic Servo
  J2 = Basic Servo
  J3 = Basic Servo
  J4 = Basic Servo
  J5 = Basic Servo
  Part2 = 16-Channel 12-bit PWM Servo Driver - I2C [part_number=815]
  A1 = DM860A Stepper Motor Driver
  M1 = Stepper Motor - Bipolar
  HLK-PM1 = HLK-PM12 [part_number=HLK-PM12]
  HC-SR04_Sensor_1 = HC-SR04 Ultrasonic Distance Sensor
  HC-SR04_Sensor_2 = HC-SR04 Ultrasonic Distance Sensor
  HC-SR04_Sensor_3 = HC-SR04 Ultrasonic Distance Sensor
  HC-SR04_Sensor_4 = HC-SR04 Ultrasonic Distance Sensor
  M2 = RioRand LM2596
  M3 = RioRand LM2596
  M4 = RioRand LM2596

nets:
  N1: Part1.D21/SCL, Part2.SCL
  N2: Part1.D20/SDA, Part2.SDA
  N3: Part1.GND, M3.Pin_4
  N4: Part1.VIN, M3.Pin_3
  N5: Part1.D2_PWM, Part2.OE
  N6: Part1.D3_PWM, A1.PUL+(+5V)
  N7: Part1.D4_PWM, A1.DIR+(+5V)
  N8: Part1.D5_PWM, A1.ENBL+(+5V)
  GND: J1.gnd, J2.gnd, J3.gnd, J4.gnd, J5.gnd, Part2.GND, M4.Pin_4
  VCC: J1.vcc, J2.vcc, J3.vcc, J4.vcc, J5.vcc, Part2.5.0V
  N9: J1.pulse, Part2.PWM15
  N10: J2.pulse, Part2.PWM13
  N11: J3.pulse, Part2.PWM14
  N12: J4.pulse, Part2.PWM11
  N13: J5.pulse, Part2.PWM12
  N14: Part2.VCC, M4.Pin_3
  N15: A1.B-, M1.D
  N16: A1.B+, M1.B
  N17: A1.A-, M1.C
  N18: A1.A+, M1.A
  N19: A1.ENBL-(ENB), A1.DIR-(DIR), A1.PUL-(PUL)
  N20: HLK-PM1.-Vo, M2.Pin_2, M3.Pin_2
  N21: HLK-PM1.+Vo, M2.Pin_1, M3.Pin_1
  VCC_2: HC-SR04_Sensor_1.VCC, HC-SR04_Sensor_2.VCC, HC-SR04_Sensor_3.VCC, HC-SR04_Sensor_4.VCC, M2.Pin_3
  GND_2: HC-SR04_Sensor_1.GND, HC-SR04_Sensor_2.GND, HC-SR04_Sensor_3.GND, HC-SR04_Sensor_4.GND, M2.Pin_4

custom parts:
  16-Channel 12-bit PWM Servo Driver - I2C: You want to make a cool robot, maybe a hexapod walker, or maybe just a piece of art with a lot of moving parts. Or maybe you want to drive a lot of LEDs with precise PWM output. Using only two pins, control 16 free-running PWM outputs! You can even chain up 62 breakouts to control up to 992 PWM outputs.
  DM860A Stepper Motor Driver: DM860A is a type of two-phase hybrid stepping motor driver, The drive voltage of which is from 24VDC to 80VDC. It is designed for use with 2-phase hybrid stepper motor of all kinds with 57mm to 110mm outside diameter and less than 8.0A phase current. Mar 2023: Correct pcb layerId as the part won't save correctly in a .fzz file as is.
